# Fritzing sketch myRFDevicesHub (saved by Fritzing 0.9.3b)
breadboards: 1

parts:
  R1 = Resistor [tolerance=±5% resistance=220 package="1206 [SMD]"]
  WeMos_D1_Mini1 = WeMos D1 Mini
  LED1 = smd LED [color="Red (633nm)" package="0603 [SMD]"]
  LED2 = smd LED [color="Blue (430nm)" package="0603 [SMD]"]
  LED3 = smd LED [color="Yellow (595nm)" package="0603 [SMD]"]
  U1 = RF-LINK_RX [package=rf-link_rx]
  S1 = Round Pushbutton

nets:
  N1: R1.Pin_0, LED1.cathode, LED2.cathode, LED3.cathode
  N2: R1.Pin_1, WeMos_D1_Mini1.G, U1.GND, S1.leg1
  5V: WeMos_D1_Mini1.5V, U1.+5V
  N3: WeMos_D1_Mini1.D2, LED2.anode
  N4: WeMos_D1_Mini1.D3, LED3.anode
  N5: WeMos_D1_Mini1.D4, LED1.anode
  N6: WeMos_D1_Mini1.D5, U1.DATA
  N7: WeMos_D1_Mini1.RST, S1.leg0

notes:
  I used Wemos D1R2 not as shown
  I used the usual 13.560 aliexpress 433Mhz RF receiver
  optional reset button
  Optional control leds:
  Error (red)
  Network Activity (yellow)
  Keep alive (blinking blue)
